# Fritzing sketch Lampada_LED_WIFI_HW (saved by Fritzing 0.9.3b)
circuit board: 3.5cm x 6cm
breadboards: 1

parts:
  U1 = ESP8266 WiFi Module [part_number=ESP8266]
  S3 = Tactile Switch Buttons - 12mm Square [package=tactile-pth-12mm]
  R3 = Resistor [tolerance=±5% resistance=470 package=THT]
  Q3 = TIP120 Hi-Current Darlington Transistor
  3_3V = screw terminal, 2 pins
  0V-100V_DC = screw terminal, 2 pins
  U2 = Luxeon LED [package=luxeon]

nets:
  3.3V: U1.VCC, U1.CH_PD, 3_3V.pin2
  N1: U1.GPIO_0, S3.1, S3.3
  N2: U1.GPIO_2, R3.Pin_0
  GND: U1.GND, S3.2, S3.4, Q3.EMITTER, 3_3V.pin1, 0V-100V_DC.pin1
  N3: R3.Pin_1, Q3.BASE
  N4: Q3.COLLECTOR, U2.C
  N5: 0V-100V_DC.pin2, U2.A

custom parts:
  ESP8266 WiFi Module: Generic WiFi Module based on the ESP8266 with onboard PCB antenna and UART communications
  Tactile Switch Buttons - 12mm Square: Medium-sized clicky momentary switches are standard input "buttons" on electronic projects. These work best in a PCB but can be used on a solderless breadboard as shown in this tutorial. The pins are normally open (disconnected) and when the button is pressed they are momentarily closed. They come in a pack of 10, they're pretty handy so you'll want to keep them around. You can find an EAGLE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
